// Digital circuit mode_selector.dig as structural Verilog
module mode_selector (
  input  ID,
  input  PWD,
  input  DIS,
  input  RESET,
  input  CLK,
  input  RST,
  output IDO,
  output PWDO
);

  wire and_1_out, and_2_out, or_1_out;

  and and_1 (and_1_out, ID, ~DIS);  // And
  and and_2 (and_2_out, PWD, ~DIS);  // And
  or or_1 (or_1_out, RESET, ~RST);  // Or
  JK_FF_AS jk_ff_as_1 (.Set(1'b0), .J(and_2_out), .C(CLK), .K(and_1_out), .Clr(or_1_out), .Q(PWDO), .nQ(IDO));
endmodule
