// Digital circuit shifter_pwd.dig as structural Verilog
module shifter_pwd (
  input  [3:0] DATA_in,
  input  [15:0] PWD_in,
  input  EN,
  input  DA,
  input  CLK,
  input  RST,
  output MATCH,
  output LED1,
  output LED2,
  output LED3,
  output LED4
);

  wire comparator_1_eq, multiplexer_1_out, multiplexer_3_out, multiplexer_5_out, multiplexer_7_out,
       register_1_q, register_3_q, register_5_q, register_7_q;
  wire [3:0] multiplexer_2_out, multiplexer_4_out, multiplexer_6_out, multiplexer_8_out, register_2_q;
  wire [15:4] register_4_q;

  Multiplexer multiplexer_1 (.sel(DA), .in_0(LED1), .in_1(DA), .out(multiplexer_1_out));
  Multiplexer #(.Bits(4)) multiplexer_2 (.sel(DA), .in_0(register_2_q), .in_1(DATA_in), .out(multiplexer_2_out));
  and and_1 (LED1, EN, register_1_q);
  Register register_1 (.D(multiplexer_1_out), .C(CLK), .en(RST), .Q(register_1_q));
  Register #(.Bits(4)) register_2 (.D(multiplexer_2_out), .C(CLK), .en(RST), .Q(register_2_q));
  Multiplexer multiplexer_3 (.sel(DA), .in_0(LED2), .in_1(register_1_q), .out(multiplexer_3_out));
  Register register_3 (.D(multiplexer_3_out), .C(CLK), .en(RST), .Q(register_3_q));
  Multiplexer #(.Bits(4)) multiplexer_4 (
    .sel(DA), .in_0(register_4_q[7:4]), .in_1(register_2_q), .out(multiplexer_4_out));
  and and_2 (LED2, EN, register_3_q);
  Register #(.Bits(4)) register_4 (.D(multiplexer_4_out), .C(CLK), .en(RST), .Q(register_4_q[7:4]));
  Multiplexer multiplexer_5 (.sel(DA), .in_0(LED3), .in_1(register_3_q), .out(multiplexer_5_out));
  Multiplexer #(.Bits(4)) multiplexer_6 (
    .sel(DA), .in_0(register_4_q[11:8]), .in_1(register_4_q[7:4]), .out(multiplexer_6_out));
  and and_3 (LED3, EN, register_5_q);
  Register register_5 (.D(multiplexer_5_out), .C(CLK), .en(RST), .Q(register_5_q));
  Register #(.Bits(4)) register_6 (.D(multiplexer_6_out), .C(CLK), .en(RST), .Q(register_4_q[11:8]));
  Multiplexer multiplexer_7 (.sel(DA), .in_0(LED4), .in_1(register_5_q), .out(multiplexer_7_out));
  Comparator #(.Signed("true"), .Bits(16)) comparator_1 (
    .a({register_4_q, register_2_q}), .b(PWD_in), .eq(comparator_1_eq));  // open: gt, lt
  Register register_7 (.D(multiplexer_7_out), .C(CLK), .en(RST), .Q(register_7_q));
  Multiplexer #(.Bits(4)) multiplexer_8 (
    .sel(DA), .in_0(register_4_q[15:12]), .in_1(register_4_q[11:8]), .out(multiplexer_8_out));
  and and_4 (LED4, EN, register_7_q);
  Register #(.Bits(4)) register_8 (.D(multiplexer_8_out), .C(CLK), .en(RST), .Q(register_4_q[15:12]));
  and and_5 (MATCH, register_7_q, comparator_1_eq);
endmodule
