// Digital circuit timer.dig as structural Verilog
module timer (
  input  START,
  input  CLK,
  input  RST,
  output RESET,
  output DIS
);

  wire and_1_out;
  wire [7:0] add_1_s, register_1_q;

  Register #(.Bits(8)) register_1 (.D(add_1_s), .C(CLK), .en(RST), .Q(register_1_q));
  Add #(.Bits(8)) add_1 (.a(8'h1), .b(register_1_q), .c_i(1'b0), .s(add_1_s));  // open: c_o
  and and_1 (and_1_out, add_1_s[0], add_1_s[1], add_1_s[2], add_1_s[3], add_1_s[4], add_1_s[5], add_1_s[6], add_1_s[7]);
  Demultiplexer demultiplexer_1 (.sel(and_1_out), .in(START), .out_0(DIS), .out_1(RESET));
endmodule
